# Fritzing sketch stoplicht (saved by Fritzing 0.9.3b)
breadboards: 1

parts:
  Onderdeel1 = Arduino Uno (Rev3)
  LED1 = LED - 5mm [color="Red (633nm)" package="5 mm [THT]"]
  LED2 = LED - 5mm [color="Green (570nm)" package="5 mm [THT]"]
  LED3 = LED - 5mm [color="Red (633nm)" package="5 mm [THT]"]
  LED4 = LED - 5mm [color="Green (570nm)" package="5 mm [THT]"]
  LED5 = LED - 5mm [color="Red (633nm)" package="5 mm [THT]"]
  LED6 = LED - 5mm [color="Green (570nm)" package="5 mm [THT]"]
  LED7 = LED - 5mm [color="Red (633nm)" package="5 mm [THT]"]
  LED8 = LED - 5mm [color="Green (570nm)" package="5 mm [THT]"]
  LED9 = LED - 5mm [color="Green (570nm)" package="5 mm [THT]"]
  S1 = Pushbutton [package="[THT]"]
  S2 = Pushbutton [package="[THT]"]
  R2 = Resistor [tolerance=±5% resistance=220 package=THT]
  R3 = Resistor [tolerance=±5% resistance=220 package=THT]
  R4 = Resistor [tolerance=±5% resistance=220 package=THT]
  R5 = Resistor [tolerance=±5% resistance=220 package=THT]

nets:
  N1: Onderdeel1.D8, LED6.anode
  N2: Onderdeel1.D9_PWM, LED5.anode
  N3: Onderdeel1.D10_PWM/SS, LED4.anode
  N4: Onderdeel1.D11_PWM/MOSI, LED3.anode
  N5: Onderdeel1.D12/MISO, LED2.anode
  N6: Onderdeel1.D13/SCK, LED1.anode
  N7: Onderdeel1.D3_PWM, S1.Pin_3, S1.Pin_4, R3.Pin_1
  N8: Onderdeel1.D4, S2.Pin_3, S2.Pin_4
  N9: Onderdeel1.D5_PWM, LED9.anode
  N10: Onderdeel1.D6_PWM, LED8.anode
  N11: Onderdeel1.D7, LED7.anode
  N12: Onderdeel1.3V3, S1.Pin_1, S1.Pin_2, S2.Pin_1, S2.Pin_2
  N13: Onderdeel1.GND, LED1.cathode, LED3.cathode, LED5.cathode, LED7.cathode, R2.Pin_0, R3.Pin_0, R4.Pin_0
  N14: LED2.cathode, LED4.cathode, LED6.cathode, LED8.cathode, LED9.cathode, R5.Pin_0
  N15: R4.Pin_1, R5.Pin_1
